# Fritzing sketch Untitled Sketch 2 (saved by Fritzing 0.9.3b)
breadboards: 1

parts:
  U1 = LCD-16X2 [package=lcd-16x2]
  Componente1 = Arduino Uno (Rev3)
  R1 = Rotary Potentiometer (Small) [maximum_resistance=100kΩ package=THT]
  R2 = Photocell (LDR) [package=THT]  # not connected

nets:
  VSS: U1.VSS, U1.R_W, U1.K, Componente1.GND
  VDD: U1.VDD, U1.A, Componente1.5V, R1.leg1, R1.leg2
  N1: U1.VO, R1.wiper
  N2: U1.RS, Componente1.D12/MISO
  N3: U1.DB4, Componente1.D5_PWM
  N4: U1.DB5, Componente1.D4
  N5: U1.DB6, Componente1.D3_PWM
  N6: U1.DB7, Componente1.D2
